# Fritzing sketch forkdroid (saved by Fritzing 0.9.4)

parts:
  MCU1 = Raspberry Pi Zero
  PWM1 = PCA9685 16x12-bit PWM Breakout
  J4 = Basic Servo
  M1 = RioRand LM2596
  VCC1 = Battery  # not connected
  J5 = Basic Servo
  J6 = Basic Servo
  J8 = Basic Servo
  J9 = Basic Servo
  S1 = Taiway 100-SP-X-T1 SPDT Miniature Toggle Switch [part_number=100-SP-X-T1-0-0-B1-M2 package=THT]
  VCC2 = Battery

nets:
  N1: MCU1.pin_1, PWM1.no_name_yet#505
  N2: MCU1.pin_3, PWM1.no_name_yet#504
  N3: MCU1.pin_4, M1.Pin_3
  N4: MCU1.pin_5, PWM1.no_name_yet#503
  N5: MCU1.pin_6, MCU1.pin_9, MCU1.pin_39, PWM1.no_name_yet#501, PWM1.no_name_yet#701, PWM1.no_name_yet#1000, PWM1.no_name_yet#1001, PWM1.no_name_yet#1007, PWM1.no_name_yet#1012, PWM1.no_name_yet#1015, M1.Pin_2, M1.Pin_4, S1.L1
  N6: PWM1.no_name_yet#0, J9.pulse
  N7: PWM1.no_name_yet#1, J8.pulse
  N8: PWM1.no_name_yet#7, J6.pulse
  N9: PWM1.no_name_yet#12, J5.pulse
  N10: PWM1.no_name_yet#15, J4.pulse
  N11: PWM1.no_name_yet#100, PWM1.no_name_yet#101, PWM1.no_name_yet#107, PWM1.no_name_yet#112, PWM1.no_name_yet#115, PWM1.no_name_yet#706, VCC2.+
